# Fritzing sketch rc_boat (saved by Fritzing 0.9.3b)
perfboards: 1

parts:
  M1 = DC Motor
  VCC3 = 4 x AA Battery Mount
  Part1 = Arduino Nano (Rev3.0)
  LED1 = LED - 3mm [color="Red (633nm)" package="3 mm [THT]"]
  IC1 = L293D [package=THT]
  J1 = Basic Servo
  ANT1 = Antenna
  U1 = RF-LINK_TX [part_number="RF receiver 433mhz" package=rf-link_tx]
  J2 = Buzzer

nets:
  N1: M1.pin_1, IC1.Out_1_(_Controlled_by_Enable_1_)
  N2: M1.pin_2, IC1.Out_2_(_Controlled_by_Enable_1_)
  N3: VCC3.-, Part1.GND, IC1.0V, J2.pin1
  N4: VCC3.+, Part1.VIN, IC1.+Vmotor
  N5: Part1.D2, IC1.In_1
  N6: Part1.D3, J1.pulse
  N7: Part1.D4, IC1.In_2
  N8: Part1.D5, LED1.anode
  N9: Part1.D6, IC1.Enable_1
  N10: Part1.D9, J2.pin2
  N11: Part1.D11/MOSI, U1.DATA
  N12: Part1.5V, IC1.+V
  N13: ANT1.antenna_lead, U1.ANT

custom parts:
  4 x AA Battery Mount: A 4 x AA battery pack (4.8 Volts with recharables)
  RF-LINK_TX: RF Link transmitters WRL-8945, 8946
  Buzzer: Fixed frequency buzzer
